# Fritzing sketch GPSSensor (saved by Fritzing 0.9.3b)

parts:
  Componente1 = Arduino Pro Mini v13
  GPS1 = Adafruit Ultimate GPS Breakout
  R1 = Resistor [tolerance=±5% resistance=150 package=THT]
  R2 = Resistor [tolerance=±5% resistance=150 package=THT]
  LED2 = LED - 3mm [color="Green (555nm)" package="3 mm [THT]"]
  LED1 = LED - 3mm [color="Red (633nm)" package="3 mm [THT]"]

nets:
  GND: Componente1.GND, GPS1.GND
  VCC: Componente1.VCC, GPS1.VIN
  N1: Componente1.D6_PWM, R1.Pin_1
  N2: Componente1.D5_PWM, R2.Pin_1
  N3: Componente1.D3_PWM, GPS1.TX
  N4: Componente1.D2, GPS1.RX
  N5: R1.Pin_0, LED1.anode
  N6: R2.Pin_0, LED2.anode

notes:
  GND
  GPS Data
  I2C Data Read
  Lego cable Blue - SDA
  Lego cable Yellow - SCL
  Lego cable Red - GND
  Lego cable Green - Vcc
