# Fritzing sketch humiditySensor (saved by Fritzing 0.9.3b)

parts:
  Componente2 = HTU21D-F Temperature + Humidity Sensor
  IC1 = Voltage Regulator AMS1117 [package=sot223]
  C1 = Ceramic Capacitor [capacitance=100nF package="100 mil [THT, multilayer]"]
  R3 = Resistor [tolerance=±5% resistance=82 package=THT]
  R2 = Resistor [tolerance=±5% resistance=82 package=THT]
  C2 = Electrolytic Capacitor [capacitance=0.1mF package="200 mil [THT, electrolytic]"]

nets:
  N1: Componente2.+3V3, IC1.OUT
  GND: Componente2.GND, IC1.GND, C1.0, C2.-
  N2: Componente2.SDA, R3.Pin_0
  N3: Componente2.SCL, R2.Pin_0
  5V: IC1.IN, C1.1
  N4: R3.Pin_1, R2.Pin_1

notes:
  82K
  Lego cable Green
  Lego cable Red + Black
  Lego cable Blue
  Lego cable Yellow
  a_ev3_cte, Humidity I2C Sensor, 1.0

custom parts:
  HTU21D-F Temperature + Humidity Sensor: This I2C digital humidity sensor is an accurate and intelligent alternative to the much simpler Humidity and Temperature Sensor - SHT15 Breakout It has a typical accuracy of ±2% with an operating range that's optimized from 5% to 95% RH. Operation outside this range is still possible - just the accuracy might drop a bit. The temperature output has an accuracy of ±1°C from -30~90°C. If you're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
